# Fritzing sketch Scheme (saved by Fritzing 0.7.7b)
breadboards: 1

parts:
  Arduino1 = Arduino
  R1 = Resistor [tolerance=±5% resistance=220 package=THT]
  LED1 = LED - 5mm [color="Red (633nm)" package="5 mm [THT]"]  # not connected
  S1 = Pushbutton [package="[THT]"]
  R2 = Resistor [tolerance=±5% resistance=10k package=THT]

nets:
  N1: Arduino1.D10, R1.Pin_0
  N2: Arduino1.D3, S1.Pin_1, S1.Pin_2, R2.Pin_1
  N3: Arduino1.+5V, R2.Pin_0
  N4: Arduino1.GND, S1.Pin_3, S1.Pin_4

notes:
  10k res
  220 res
